// Logisim project cpu.circ as structural Verilog: 1 circuit, main circuit main
module main (
  input  [31:0] INSTRUCTION,
  input  CLOCK,
  output [31:0] PROGRAM_COUNTER,
  output [31:0] ra,
  output [31:0] sp,
  output [31:0] t0,
  output [31:0] t1,
  output [31:0] t2,
  output [31:0] s0,
  output [31:0] s1,
  output [31:0] a0
);

  wire [1:0] WBSel;
  wire [2:0] funct3;
  wire [11:0] instruction_fetched;
  wire [31:0] adder_1_out, alu_result, imm, instrcution_fetched, read_data, rs1value, writeback_value;

  control_logic control_logic_1 (.WBSel(WBSel));  // open: BSel, BrUn, RegWEn, ImmSel, ASel, PCSel, BrLt, BrEq, inst, ALUSel, MemRW
  Adder #(.width(32)) adder_1 (.a(PROGRAM_COUNTER), .b(32'h4), .out(adder_1_out));  // open: cin, cout
  Register #(.width(32)) PC (.D(adder_1_out), .clk(CLOCK), .Q(PROGRAM_COUNTER));  // open: en, clr
  // imm_gen imm_gen_1: pin names not known; wires that end beside it: instruction_fetched, imm
  Multiplexer #(.select(2), .width(32), .enable("false")) multiplexer_1 (
    .in0(alu_result), .in1(read_data), .out(writeback_value), .sel(2'b00));  // open: in2, in3
  // branch_comp branch_comp_1: pin names not known
  Register #(.width(32)) register_1 (
    .D(INSTRUCTION), .clk(CLOCK), .Q({instrcution_fetched[31:15], funct3, instrcution_fetched[11:0]}));  // open: en, clr
  regfile_main RegFile (
    .rd(instrcution_fetched[11:7]), .Read_Data_1(rs1value), .ra(ra), .sp(sp), .t0(t0), .t1(t1), .t2(t2),
    .s0(s0), .s1(s1), .a0(a0), .rs1(instrcution_fetched[19:15]), .Write_Data(writeback_value), .RegWEn(1'b1),
    .clk(CLOCK));  // open: rs2, Read_Data_2
  alu Arithmetic_Logic_Unit (.Result(alu_result), .ALUSel(4'b0000), .A(rs1value), .B(imm));
  // mem_main DMEM: pin names not known; wires that end beside it: CLOCK, read_data

  // Other names for the same wires on the sheet: clk = CLOCK; opcode[6:0] = instrcution_fetched[6:0];
  //   rd[4:0] = instrcution_fetched[11:7]; instrcution_fetched[14:12] = funct3; rs1[4:0] = instrcution_fetched[19:15]

  // Notes on the sheet:
  //   Output
  //   IMEM (do **NOT** move this)
  //   Inputs
  //   It is OK to move the PC, RegFile, ALU, MEM, Branch Comp, Imm Gen, and Control Logic to wherever is most convenient for you when constructing your CPU, and to delete this text
  //   Inputs/Outputs for testing. Do **NOT** move these.
endmodule
